// Digital circuit CPU.dig as structural Verilog
module CPU (
  input  clk
);

  wire A_LD_CDATA, A_OUT_CDATA, ALU_OUT_CDATA, ALUA_LD_CDATA, ALUB_LD_CDATA, ALUOP_0, ALUOP_1, ALUOP_2,
       and_1_out, and_2_out, and_3_out, CDATA_TO_CADDRH, CDATA_TO_CADDRL, IR_LD_XDATA, MARH_LD_CADDRH,
       MARL_LD_CADDRL, MBR_LD_CDATA, MBR_LD_XDATA, MBR_OUT_CDATA, MBR_OUT_XDATA, MEM_LD_XDATA, MEM_OUT_XDATA,
       not_1_out, or_1_out, or_2_out, or_3_out, or_4_out, PC_INC, PC_OUT_CADDR, PCADDL_c_o, PCH_LD_CADDRH,
       PCL_LD_CADDRL, STASH_LD_CDATA, STASH_OUT_CDATA, X_LD_CDATA, X_OUT_CDATA, Y_LD_CDATA, Y_OUT_CDATA;
  wire [7:0] A, ALUA, ALUB, ALUR, driver_1_out, driver_2_out, driver_6_out, IR, MARH, MARL, MBR,
       multiplexer_1_out, multiplexer_2_out, multiplexer_3_out, PCADDH_s, PCADDL_s, PCH, PCL, ROM_d, STASH,
       X, Y;

  Seven_Seg_Hex seven_seg_hex_1 (.d(MARH[7:4]), .dp(1'b0));
  Seven_Seg_Hex seven_seg_hex_2 (.d(A[7:4]), .dp(1'b0));
  Seven_Seg_Hex seven_seg_hex_3 (.d(MARL[7:4]), .dp(1'b0));
  Seven_Seg_Hex seven_seg_hex_4 (.d(MARH[3:0]), .dp(1'b0));
  Seven_Seg_Hex seven_seg_hex_5 (.d(A[3:0]), .dp(1'b0));
  Seven_Seg_Hex seven_seg_hex_6 (.d(X[7:4]), .dp(1'b0));
  Seven_Seg_Hex seven_seg_hex_7 (.d(MBR[7:4]), .dp(1'b0));
  Seven_Seg_Hex seven_seg_hex_8 (.d(MARL[3:0]), .dp(1'b0));
  Seven_Seg_Hex seven_seg_hex_9 (.d(X[3:0]), .dp(1'b0));
  Multiplexer #(.Bits(8)) multiplexer_1 (.sel(PC_INC), .in_0(driver_1_out), .in_1(PCADDH_s), .out(multiplexer_1_out));
  Seven_Seg_Hex seven_seg_hex_10 (.d(MBR[3:0]), .dp(1'b0));
  Seven_Seg_Hex seven_seg_hex_11 (.d(Y[3:0]), .dp(1'b0));
  Seven_Seg_Hex seven_seg_hex_12 (.d(Y[7:4]), .dp(1'b0));
  Seven_Seg_Hex seven_seg_hex_13 (.d(PCH[3:0]), .dp(1'b0));
  Seven_Seg_Hex seven_seg_hex_14 (.d(PCH[7:4]), .dp(1'b0));
  or or_1 (or_1_out, PC_INC, PCH_LD_CADDRH);
  Add #(.Bits(8)) PCADDH (.a(PCH), .b({8{1'b0}}), .c_i(PCADDL_c_o), .s(PCADDH_s));  // open: c_o
  Seven_Seg_Hex seven_seg_hex_15 (.d(PCL[3:0]), .dp(1'b0));
  Seven_Seg_Hex seven_seg_hex_16 (.d(PCL[7:4]), .dp(1'b0));
  Seven_Seg_Hex seven_seg_hex_17 (.d(ALUA[3:0]), .dp(1'b0));
  Seven_Seg_Hex seven_seg_hex_18 (.d(ALUA[7:4]), .dp(1'b0));
  Register #(.Bits(8)) u_PCH (.D(multiplexer_1_out), .C(clk), .en(or_1_out), .Q(PCH));
  Seven_Seg_Hex seven_seg_hex_19 (.d(IR[3:0]), .dp(1'b0));
  Seven_Seg_Hex seven_seg_hex_20 (.d(IR[7:4]), .dp(1'b0));
  Seven_Seg_Hex seven_seg_hex_21 (.d(ALUB[3:0]), .dp(1'b0));
  Seven_Seg_Hex seven_seg_hex_22 (.d(ALUB[7:4]), .dp(1'b0));
  Seven_Seg_Hex seven_seg_hex_23 (.d(STASH[7:4]), .dp(1'b0));
  Seven_Seg_Hex seven_seg_hex_24 (.d(ALUR[7:4]), .dp(1'b0));
  assign driver_1_out = PC_OUT_CADDR ? PCH : 8'bz;  // Driver driver_1
  Seven_Seg_Hex seven_seg_hex_25 (.d(STASH[3:0]), .dp(1'b0));
  Seven_Seg_Hex seven_seg_hex_26 (.d(ALUR[3:0]), .dp(1'b0));
  Multiplexer #(.Bits(8)) multiplexer_2 (.sel(PC_INC), .in_0(driver_2_out), .in_1(PCADDL_s), .out(multiplexer_2_out));
  or or_2 (or_2_out, PC_INC, PCL_LD_CADDRL);
  Add #(.Bits(8)) PCADDL (.a(PCL), .b(8'h1), .c_i(1'b0), .s(PCADDL_s), .c_o(PCADDL_c_o));
  Register #(.Bits(8)) u_PCL (.D(multiplexer_2_out), .C(clk), .en(or_2_out), .Q(PCL));
  Register #(.Bits(8)) MAR_H (.D(driver_1_out), .C(clk), .en(MARH_LD_CADDRH), .Q(MARH));
  assign driver_2_out = PC_OUT_CADDR ? PCL : 8'bz;  // Driver driver_2
  Register #(.Bits(8)) MAR_L (.D(driver_2_out), .C(clk), .en(MARL_LD_CADDRL), .Q(MARL));
  assign driver_2_out = CDATA_TO_CADDRL ? driver_6_out : 8'bz;  // Driver driver_3
  assign driver_1_out = CDATA_TO_CADDRH ? driver_6_out : 8'bz;  // Driver driver_4
  and and_1 (and_1_out, MARH[7], MEM_OUT_XDATA);
  Multiplexer #(.Bits(8)) multiplexer_3 (
    .sel(MBR_LD_CDATA), .in_0(ROM_d), .in_1(driver_6_out), .out(multiplexer_3_out));
  Register #(.Bits(8)) u_MBR (.D(multiplexer_3_out), .C(clk), .en(or_3_out), .Q(MBR));
  or or_3 (or_3_out, MBR_LD_CDATA, MBR_LD_XDATA);
  not not_1 (not_1_out, MARH[7]);
  ROM #(.AddrBits(14), .Bits(8)) ROM (.A({MARH[5:0], MARL}), .sel(and_1_out), .D(ROM_d));
  or or_4 (or_4_out, MEM_LD_XDATA, MEM_OUT_XDATA);
  assign ROM_d = MBR_OUT_XDATA ? MBR : 8'bz;  // Driver driver_5
  assign driver_6_out = MBR_OUT_CDATA ? MBR : 8'bz;  // Driver driver_6
  Register #(.Bits(8)) u_ALUB (.D(driver_6_out), .C(clk), .en(ALUB_LD_CDATA), .Q(ALUB));
  and and_2 (and_2_out, or_4_out, not_1_out);
  and and_3 (and_3_out, MEM_LD_XDATA, clk);
  Register #(.Bits(8)) u_IR (.D(ROM_d), .C(clk), .en(IR_LD_XDATA), .Q(IR));
  Register #(.Bits(8)) u_ALUA (.D(driver_6_out), .C(clk), .en(ALUA_LD_CDATA), .Q(ALUA));
  RAMSinglePortSel #(.AddrBits(14), .isProgramMemory("true"), .Bits(8)) RAM (
    .A({MARH[5:0], MARL}), .CS(and_2_out), .WE(and_3_out), .OE(MEM_OUT_XDATA), .D(ROM_d));
  ALU alu_1 (
    .A(ALUA), .B(ALUB), .OP({ALUOP_2, ALUOP_1, ALUOP_0}), .Nin(1'b0), .Zin(1'b0), .Cin(1'b0), .Vin(1'b0),
    .Out(ALUR));  // open: Nout, Zout, Cout, Vout
  Register #(.Bits(8)) u_STASH (.D(driver_6_out), .C(clk), .en(STASH_LD_CDATA), .Q(STASH));
  assign driver_6_out = ALU_OUT_CDATA ? ALUR : 8'bz;  // Driver driver_7
  assign driver_6_out = STASH_OUT_CDATA ? STASH : 8'bz;  // Driver driver_8
  Register #(.Bits(8)) u_A (.D(driver_6_out), .C(clk), .en(A_LD_CDATA), .Q(A));
  Control_Unit control_unit_1 (
    .Nin(1'b0), .Vin(1'b0), .Zin(1'b0), .Cin(1'b0), .IRin(IR), .ClockIn(clk), .HALT(PC_OUT_CADDR),
    .MEM_LD_XDATA(MARH_LD_CADDRH), .MEM_OUT_XDATA(IR_LD_XDATA), .IR_LD_XDATA(PC_INC),
    .MBR_LD_XDATA(MBR_LD_XDATA), .MBR_OUT_XDATA(MBR_OUT_CDATA), .MBR_LD_CDATA(A_LD_CDATA),
    .MBR_OUT_CDATA(MEM_OUT_XDATA), .MARL_LD_CADDRL(MEM_LD_XDATA), .MARH_LD_CADDRH(MBR_OUT_XDATA),
    .PCL_LD_CDATA(MBR_LD_CDATA), .PCH_LD_CDATA(A_OUT_CDATA), .PC_INC(MARL_LD_CADDRL),
    .PC_LD_ADD(CDATA_TO_CADDRH), .PC_OUT_CADDR(CDATA_TO_CADDRL), .PCL_LD_CADDRL(STASH_LD_CDATA),
    .PCH_LD_CADDRH(STASH_OUT_CDATA), .STASHH_LD_CDATA(PCL_LD_CADDRL), .STASHH_OUT_CDATA(PCH_LD_CADDRH),
    .A_LD_CDATA(ALUA_LD_CDATA), .A_OUT_CDATA(ALU_OUT_CDATA), .X_LDCDATA(ALUOP_0), .X_OUT_CDATA(ALUOP_1),
    .Y_LD_CDATA(ALUOP_2), .Y_OUT_CDATA(ALUB_LD_CDATA), .PN_LD(X_LD_CDATA), .PV_LD(Y_LD_CDATA),
    .PZ_LD(X_OUT_CDATA), .PC_LD(Y_OUT_CDATA));  // open: RESET, P_SRC_0, P_SRC_1, ALUA_LD_CDATA, ALU_B_LD_CDATA, ALUP_LD_P, ALUR_OUT_CDATA, ALU_OP_0, ALU_OP_1, ALU_OP_2, lt_CAR_gt, lt_UNEXTADDR_gt, lt_NEXT_gt, lt_NEXTMUX_gt, lt_MODEMAP_gt, lt_OPCODEMAP_gt, S_INC, S_DEC, S_OUT_ADDR, S_LD_CDATA, CDATA_LD_0, CDATA_LD_FF, S_OUT_CDATA, PCL_OUT_CDATA, PCH_OUT_CDATA, STASHL_LD_CDATA, STASHL_OUT_CDATA, CDATA_TO_CADDRL, CDATA_TO_CADDRH
  assign driver_6_out = A_OUT_CDATA ? A : 8'bz;  // Driver driver_9
  Register #(.Bits(8)) u_X (.D(driver_6_out), .C(clk), .en(X_LD_CDATA), .Q(X));
  assign driver_6_out = X_OUT_CDATA ? X : 8'bz;  // Driver driver_10
  Register #(.Bits(8)) u_Y (.D(driver_6_out), .C(clk), .en(Y_LD_CDATA), .Q(Y));
  assign driver_6_out = Y_OUT_CDATA ? Y : 8'bz;  // Driver driver_11

  // Other names for the same wires on the sheet: P0_Clock = clk

  // Notes on the sheet:
  //   clk: Hz: 100
  //   MAR
  //   A
  //   CADDRH Bus
  //   X
  //   MBR
  //   Y
  //   PC
  //   ALUA
  //   IR
  //   ALUB
  //   ALUOUT
  //   CADDRL Bus
  //   STASH
  //   XADDR Bus
  //   High bit 
  //     set => ROM
  //     unset => RAM
  //   XDATA Bus
  //   CDATA Bus
  //   contents of ROM (hex, n*v repeats v):
  //   a9,42
endmodule
